# Fritzing sketch solenoidControlAnalog (saved by Fritzing 0.7.9b)
breadboards: 1

parts:
  part = Arduino  # not connected
  R1 = Resistor [tolerance=±5% resistance=220 package=THT]
  part_2 = mystery part, 3 pins [chip_label=?]  # not connected
  Q1 = Basic FET P-Channel [package="TO220 [THT]"]
  part_3 = mystery part, 3 pins [chip_label=?]  # not connected
  sol1 = Solenoid
  D1 = Rectifier Diode [part_number=1N4001 package="300 mil [THT]"]
  LED-R1 = Resistor [tolerance=±5% resistance=220 package=THT]
  LED1 = LED - 5mm [color="Red (633nm)" package="5 mm [THT]"]
  VCC1 = Battery
  R2 = Resistor [tolerance=±5% resistance=220 package=THT]
  Q2 = Basic FET P-Channel [package="TO220 [THT]"]
  sol2 = Solenoid
  D2 = Rectifier Diode [part_number=1N4001 package="300 mil [THT]"]
  LED-R2 = Resistor [tolerance=±5% resistance=220 package=THT]
  LED2 = LED - 5mm [color="Red (633nm)" package="5 mm [THT]"]
  R3 = Resistor [tolerance=±5% resistance=220 package=THT]
  Q3 = Basic FET P-Channel [package="TO220 [THT]"]
  sol3 = Solenoid
  D3 = Rectifier Diode [part_number=1N4001 package="300 mil [THT]"]
  LED-R3 = Resistor [tolerance=±5% resistance=220 package=THT]
  LED3 = LED - 5mm [color="Red (633nm)" package="5 mm [THT]"]
  R4 = Resistor [tolerance=±5% resistance=220 package=THT]
  Q4 = Basic FET P-Channel [package="TO220 [THT]"]
  sol4 = Solenoid
  D4 = Rectifier Diode [part_number=1N4001 package="300 mil [THT]"]
  LED-R4 = Resistor [tolerance=±5% resistance=220 package=THT]
  LED4 = LED - 5mm [color="Red (633nm)" package="5 mm [THT]"]
  R5 = Resistor [tolerance=±5% resistance=220 package=THT]
  Q5 = Basic FET P-Channel [package="TO220 [THT]"]
  sol5 = Solenoid
  D5 = Rectifier Diode [part_number=1N4001 package="300 mil [THT]"]
  LED-R5 = Resistor [tolerance=±5% resistance=220 package=THT]
  LED5 = LED - 5mm [color="Red (633nm)" package="5 mm [THT]"]
  R6 = Resistor [tolerance=±5% resistance=220 package=THT]
  Q6 = Basic FET P-Channel [package="TO220 [THT]"]
  sol6 = Solenoid
  D6 = Rectifier Diode [part_number=1N4001 package="300 mil [THT]"]
  LED-R6 = Resistor [tolerance=±5% resistance=220 package=THT]
  LED6 = LED - 5mm [color="Red (633nm)" package="5 mm [THT]"]
  Arduino1 = Arduino

nets:
  N1: R1.Pin_0, LED-R1.Pin_0, Arduino1.D9
  N2: R1.Pin_1, Q1.gate
  N3: Q1.drain, sol1.pin1, D1.anode
  N4: sol1.pin2, D1.cathode, VCC1.+, sol2.pin2, D2.cathode, sol3.pin2, D3.cathode, sol4.pin2, D4.cathode, sol5.pin2, D5.cathode, sol6.pin2, D6.cathode
  N5: LED-R1.Pin_1, LED1.anode
  N6: R2.Pin_0, LED-R2.Pin_0, Arduino1.D10
  N7: R2.Pin_1, Q2.gate
  N8: Q2.drain, sol2.pin1, D2.anode
  N9: LED-R2.Pin_1, LED2.anode
  N10: R3.Pin_0, LED-R3.Pin_0, Arduino1.D11
  N11: R3.Pin_1, Q3.gate
  N12: Q3.drain, sol3.pin1, D3.anode
  N13: LED-R3.Pin_1, LED3.anode
  N14: R4.Pin_0, LED-R4.Pin_0, Arduino1.D3
  N15: R4.Pin_1, Q4.gate
  N16: Q4.drain, sol4.pin1, D4.anode
  N17: LED-R4.Pin_1, LED4.anode
  N18: R5.Pin_0, LED-R5.Pin_0, Arduino1.D5
  N19: R5.Pin_1, Q5.gate
  N20: Q5.drain, sol5.pin1, D5.anode
  N21: LED-R5.Pin_1, LED5.anode
  N22: R6.Pin_0, LED-R6.Pin_0, Arduino1.D6
  N23: R6.Pin_1, Q6.gate
  N24: Q6.drain, sol6.pin1, D6.anode
  N25: LED-R6.Pin_1, LED6.anode
