# Fritzing sketch solenoidControlArduinoMega (saved by Fritzing 0.7.9b)
breadboards: 1

parts:
  U1 = Arduino Mega
  R1 = Resistor [tolerance=±5% resistance=220 package=THT]
  Q1 = Basic FET P-Channel [package="TO220 [THT]"]
  sol1 = Solenoid
  D1 = Rectifier Diode [part_number=1N4001 package="300 mil [THT]"]
  LED-R1 = Resistor [tolerance=±5% resistance=220 package=THT]
  LED1 = LED - 5mm [color="Red (633nm)" package="5 mm [THT]"]
  part = Basic FET P-Channel [package="TO220 [THT]"]  # not connected
  part_2 = Resistor [tolerance=±5% resistance=220 package=THT]  # not connected
  LED2 = LED - 5mm [color="Red (633nm)" package="5 mm [THT]"]  # not connected
  sol2 = Solenoid  # not connected
  sol3 = Solenoid  # not connected
  LED3 = LED - 5mm [color="Red (633nm)" package="5 mm [THT]"]  # not connected
  D2 = Rectifier Diode [part_number=1N4001 package="300 mil [THT]"]  # not connected
  Q2 = Basic FET P-Channel [package="TO220 [THT]"]  # not connected

nets:
  N1: U1.D22, R1.Pin_0, LED-R1.Pin_0
  N2: R1.Pin_1, Q1.gate
  N3: Q1.drain, sol1.pin1, D1.anode
  N4: sol1.pin2, D1.cathode
  N5: LED-R1.Pin_1, LED1.anode
