# Fritzing sketch solenoidControlFull (saved by Fritzing 0.7.9b)
breadboards: 1

parts:
  part = Arduino  # not connected
  R1 = Resistor [tolerance=±5% resistance=220 package=THT]
  part_2 = mystery part, 3 pins [chip_label=?]  # not connected
  Q1 = Basic FET P-Channel [package="TO220 [THT]"]
  part_3 = mystery part, 3 pins [chip_label=?]  # not connected
  sol1 = Solenoid
  D1 = Rectifier Diode [part_number=1N4001 package="300 mil [THT]"]
  LED-R1 = Resistor [tolerance=±5% resistance=220 package=THT]
  LED1 = LED - 5mm [color="Red (633nm)" package="5 mm [THT]"]
  VCC1 = Battery
  R2 = Resistor [tolerance=±5% resistance=220 package=THT]
  Q2 = Basic FET P-Channel [package="TO220 [THT]"]
  D2 = Rectifier Diode [part_number=1N4001 package="300 mil [THT]"]
  LED-R2 = Resistor [tolerance=±5% resistance=220 package=THT]
  LED2 = LED - 5mm [color="Red (633nm)" package="5 mm [THT]"]
  R3 = Resistor [tolerance=±5% resistance=220 package=THT]
  Q3 = Basic FET P-Channel [package="TO220 [THT]"]
  sol3 = Solenoid
  D3 = Rectifier Diode [part_number=1N4001 package="300 mil [THT]"]
  LED-R3 = Resistor [tolerance=±5% resistance=220 package=THT]
  LED3 = LED - 5mm [color="Red (633nm)" package="5 mm [THT]"]
  R4 = Resistor [tolerance=±5% resistance=220 package=THT]
  Q4 = Basic FET P-Channel [package="TO220 [THT]"]
  sol4 = Solenoid
  D4 = Rectifier Diode [part_number=1N4001 package="300 mil [THT]"]
  LED-R4 = Resistor [tolerance=±5% resistance=220 package=THT]
  LED4 = LED - 5mm [color="Red (633nm)" package="5 mm [THT]"]
  R5 = Resistor [tolerance=±5% resistance=220 package=THT]
  Q5 = Basic FET P-Channel [package="TO220 [THT]"]
  sol5 = Solenoid
  D5 = Rectifier Diode [part_number=1N4001 package="300 mil [THT]"]
  LED-R5 = Resistor [tolerance=±5% resistance=220 package=THT]
  LED5 = LED - 5mm [color="Red (633nm)" package="5 mm [THT]"]
  R6 = Resistor [tolerance=±5% resistance=220 package=THT]
  Q6 = Basic FET P-Channel [package="TO220 [THT]"]
  sol6 = Solenoid
  D6 = Rectifier Diode [part_number=1N4001 package="300 mil [THT]"]
  LED-R6 = Resistor [tolerance=±5% resistance=220 package=THT]
  LED6 = LED - 5mm [color="Red (633nm)" package="5 mm [THT]"]
  Arduino1 = Arduino
  sol2 = Solenoid
  R7 = Resistor [tolerance=±5% resistance=220 package=THT]
  Q7 = Basic FET P-Channel [package="TO220 [THT]"]
  sol7 = Solenoid
  D7 = Rectifier Diode [part_number=1N4001 package="300 mil [THT]"]
  LED-R7 = Resistor [tolerance=±5% resistance=220 package=THT]
  LED7 = LED - 5mm [color="Red (633nm)" package="5 mm [THT]"]
  R8 = Resistor [tolerance=±5% resistance=220 package=THT]
  Q8 = Basic FET P-Channel [package="TO220 [THT]"]
  sol8 = Solenoid
  D8 = Rectifier Diode [part_number=1N4001 package="300 mil [THT]"]
  LED-R8 = Resistor [tolerance=±5% resistance=220 package=THT]
  LED8 = LED - 5mm [color="Red (633nm)" package="5 mm [THT]"]
  R9 = Resistor [tolerance=±5% resistance=220 package=THT]
  R10 = Resistor [tolerance=±5% resistance=220 package=THT]
  Q9 = Basic FET P-Channel [package="TO220 [THT]"]
  Q10 = Basic FET P-Channel [package="TO220 [THT]"]
  sol9 = Solenoid
  D9 = Rectifier Diode [part_number=1N4001 package="300 mil [THT]"]
  D10 = Rectifier Diode [part_number=1N4001 package="300 mil [THT]"]
  LED-R9 = Resistor [tolerance=±5% resistance=220 package=THT]
  LED-R10 = Resistor [tolerance=±5% resistance=220 package=THT]
  LED9 = LED - 5mm [color="Red (633nm)" package="5 mm [THT]"]
  LED10 = LED - 5mm [color="Red (633nm)" package="5 mm [THT]"]
  R11 = Resistor [tolerance=±5% resistance=220 package=THT]
  Q11 = Basic FET P-Channel [package="TO220 [THT]"]
  sol11 = Solenoid
  D11 = Rectifier Diode [part_number=1N4001 package="300 mil [THT]"]
  LED-R11 = Resistor [tolerance=±5% resistance=220 package=THT]
  LED11 = LED - 5mm [color="Red (633nm)" package="5 mm [THT]"]
  R12 = Resistor [tolerance=±5% resistance=220 package=THT]
  Q12 = Basic FET P-Channel [package="TO220 [THT]"]
  sol12 = Solenoid
  D12 = Rectifier Diode [part_number=1N4001 package="300 mil [THT]"]
  LED-R12 = Resistor [tolerance=±5% resistance=220 package=THT]
  LED12 = LED - 5mm [color="Red (633nm)" package="5 mm [THT]"]
  sol10 = Solenoid

nets:
  N1: R1.Pin_0, LED-R1.Pin_0, Arduino1.D11
  N2: R1.Pin_1, Q1.gate
  N3: Q1.drain, sol1.pin1, D1.anode
  N4: sol1.pin2, D1.cathode, VCC1.+, D2.cathode, sol3.pin2, D3.cathode, sol4.pin2, D4.cathode, sol5.pin2, D5.cathode, sol6.pin2, D6.cathode, sol2.pin2, sol7.pin2, D7.cathode, sol8.pin2, D8.cathode, sol9.pin2, D9.cathode, D10.cathode, sol11.pin2, D11.cathode, sol12.pin2, D12.cathode, sol10.pin2
  N5: LED-R1.Pin_1, LED1.anode
  N6: R2.Pin_0, LED-R2.Pin_0, Arduino1.D12
  N7: R2.Pin_1, Q2.gate
  N8: Q2.drain, D2.anode, sol2.pin1
  N9: LED-R2.Pin_1, LED2.anode
  N10: R3.Pin_0, LED-R3.Pin_0, Arduino1.D13
  N11: R3.Pin_1, Q3.gate
  N12: Q3.drain, sol3.pin1, D3.anode
  N13: LED-R3.Pin_1, LED3.anode
  N14: R4.Pin_0, LED-R4.Pin_0, Arduino1.D8
  N15: R4.Pin_1, Q4.gate
  N16: Q4.drain, sol4.pin1, D4.anode
  N17: LED-R4.Pin_1, LED4.anode
  N18: R5.Pin_0, LED-R5.Pin_0, Arduino1.D9
  N19: R5.Pin_1, Q5.gate
  N20: Q5.drain, sol5.pin1, D5.anode
  N21: LED-R5.Pin_1, LED5.anode
  N22: R6.Pin_0, LED-R6.Pin_0, Arduino1.D10
  N23: R6.Pin_1, Q6.gate
  N24: Q6.drain, sol6.pin1, D6.anode
  N25: LED-R6.Pin_1, LED6.anode
  N26: Arduino1.D7, R9.Pin_0, LED-R9.Pin_0
  N27: Arduino1.D6, R8.Pin_0, LED-R8.Pin_0
  N28: Arduino1.D5, R7.Pin_0, LED-R7.Pin_0
  N29: Arduino1.D4, R10.Pin_0, LED-R10.Pin_0
  N30: Arduino1.D3, R12.Pin_0, LED-R12.Pin_0
  N31: Arduino1.D2, R11.Pin_0, LED-R11.Pin_0
  N32: R7.Pin_1, Q7.gate
  N33: Q7.drain, sol7.pin1, D7.anode
  N34: LED-R7.Pin_1, LED7.anode
  N35: R8.Pin_1, Q8.gate
  N36: Q8.drain, sol8.pin1, D8.anode
  N37: LED-R8.Pin_1, LED8.anode
  N38: R9.Pin_1, Q9.gate
  N39: R10.Pin_1, Q10.gate
  N40: Q9.drain, sol9.pin1, D9.anode
  N41: Q10.drain, D10.anode, sol10.pin1
  N42: LED-R9.Pin_1, LED9.anode
  N43: LED-R10.Pin_1, LED10.anode
  N44: R11.Pin_1, Q11.gate
  N45: Q11.drain, sol11.pin1, D11.anode
  N46: LED-R11.Pin_1, LED11.anode
  N47: R12.Pin_1, Q12.gate
  N48: Q12.drain, sol12.pin1, D12.anode
  N49: LED-R12.Pin_1, LED12.anode
