# Fritzing sketch solenoidControlModule (saved by Fritzing 0.7.9b)
breadboards: 1

parts:
  part = Arduino Mega  # not connected
  R2 = Resistor [tolerance=±5% resistance=220 package=THT]
  Q2 = Basic FET P-Channel [package="TO220 [THT]"]
  sol2 = Solenoid
  D2 = Rectifier Diode [part_number=1N4001 package="300 mil [THT]"]
  LED-R2 = Resistor [tolerance=±5% resistance=220 package=THT]
  LED2 = LED - 5mm [color="Red (633nm)" package="5 mm [THT]"]

nets:
  N1: R2.Pin_0, LED-R2.Pin_0
  N2: R2.Pin_1, Q2.gate
  N3: Q2.drain, sol2.pin1, D2.anode
  N4: sol2.pin2, D2.cathode
  N5: LED-R2.Pin_1, LED2.anode
